# Fritzing sketch waterer-diagram (saved by Fritzing 0.9.3b)

parts:
  Raspberry_Pi_3 = Raspberry Pi 3 [part_number=RPI-3-V1.2]
  12V_Plug = Power plug
  part = Humidity and Temperature Sensor RHT03
  part_2 = Relay [part_number=FRS1B-S package=THT]
  Solenoid = Solenoid

nets:
  N1: Raspberry_Pi_3.GPIO17, part.Data-signal
  3V3: Raspberry_Pi_3.3V3, part.Vcc
  N2: Raspberry_Pi_3.GND, part.GND_1, part_2.A, part_2.COIL1
  N3: Raspberry_Pi_3.GPIO16, part_2.COIL2
  N4: Raspberry_Pi_3.5V, part_2.B
  N5: 12V_Plug.VCC, part_2.C1, part_2.C2, Solenoid.pin2
  N6: 12V_Plug.GND, Solenoid.pin1
